# Fritzing sketch flowmeter (saved by Fritzing 0.9.4)
circuit board: 6.41646cm x 7.58437cm
breadboards: 1

parts:
  LCD1 = LCD screen
  Part1 = Arduino Board Ethernet
  R1 = Rotary Potentiometer (Small) [maximum_resistance=100kΩ package=THT]
  YF-S201_Flow_Meter1 = YF-S201 Water Flow Meter
  YF-S201_Flow_Meter2 = YF-S201 Water Flow Meter
  10k = Resistor [tolerance=±5% resistance=220 package=THT]
  10k_2 = Resistor [tolerance=±5% resistance=220 package=THT]

nets:
  GND: LCD1.VSS, LCD1.R/W, LCD1.LED+, Part1.GND, R1.leg2, YF-S201_Flow_Meter1.GND, YF-S201_Flow_Meter2.GND
  VCC: LCD1.VDD, LCD1.LED-, Part1.5V, R1.leg1, YF-S201_Flow_Meter1.VCC, YF-S201_Flow_Meter2.VCC, 10k.Pin_1, 10k_2.Pin_1
  N1: LCD1.V0, R1.wiper
  N2: LCD1.RS, Part1.D9_PWM
  N3: LCD1.E, Part1.D8
  N4: LCD1.DB4, Part1.D7
  N5: LCD1.DB5, Part1.D6_PWM
  N6: LCD1.DB6, Part1.D5_PWM
  N7: LCD1.DB7, Part1.D4
  N8: Part1.D2_PWM, YF-S201_Flow_Meter2.SIG, 10k.Pin_0
  N9: Part1.D3_PWM, YF-S201_Flow_Meter1.SIG, 10k_2.Pin_0

custom parts:
  YF-S201 Water Flow Meter: The YF-S201 Flow Meter. The input voltage is 5V to 24V (DC).
